// Logisim project Shudong-INATOR.circ as structural Verilog: 6 circuits, main circuit main
module main (
);

  wire clock_1_out, control_1_aluop, control_1_alusrc, control_1_memread, control_1_memtoreg,
       control_1_memwrite, control_1_reg2loc, control_1_regwrite;
  wire [1:0] instructionsplitter_1_opcode, instructionsplitter_1_rm, instructionsplitter_1_rn,
       instructionsplitter_1_targetreg, multiplexer_1_out;
  wire [7:0] adder_1_out, alu_1_aluout, Data_Memory_dout, instructionsplitter_1_imm8, multiplexer_2_out,
       multiplexer_3_out, multiplexer_4_out, PC_q, registerfile_1_regdata1, registerfile_1_regdata2;
  wire [15:0] Instructions_Memory_dout;

  Clock clock_1 (.out(clock_1_out));
  Register PC (.D(adder_1_out), .en(1'b1), .clk(clock_1_out), .Q(PC_q));  // open: clr
  Adder adder_1 (.a(PC_q), .b(8'h1), .out(adder_1_out));  // open: cin, cout
  RAM #(.dataWidth(16)) Instructions_Memory (
    .addr(PC_q), .we(1'b0), .oe(1'b1), .clk(clock_1_out), .dout(Instructions_Memory_dout));  // open: din
  InstructionSplitter instructionsplitter_1 (
    .Instruction(Instructions_Memory_dout), .TargetReg(instructionsplitter_1_targetreg),
    .Rn(instructionsplitter_1_rn), .Rm(instructionsplitter_1_rm), .opcode(instructionsplitter_1_opcode),
    .imm8(instructionsplitter_1_imm8));
  Control control_1 (
    .opcode(instructionsplitter_1_opcode), .MemToReg(control_1_memtoreg), .MemRead(control_1_memread),
    .MemWrite(control_1_memwrite), .ALUsrc(control_1_alusrc), .ALUop(control_1_aluop),
    .RegWrite(control_1_regwrite), .Reg2Loc(control_1_reg2loc));
  Multiplexer #(.width(2)) multiplexer_1 (
    .in0(instructionsplitter_1_rm), .in1(instructionsplitter_1_targetreg), .out(multiplexer_1_out),
    .sel(control_1_reg2loc));
  RAM Data_Memory (
    .addr(alu_1_aluout), .we(control_1_memwrite), .oe(control_1_memread), .clk(clock_1_out),
    .din(registerfile_1_regdata2), .dout(Data_Memory_dout));
  RegisterFile registerfile_1 (
    .YEPCLOCK(clock_1_out), .WriteReg(instructionsplitter_1_targetreg), .RegWrite(control_1_regwrite),
    .RegDataW(multiplexer_3_out), .ReadReg1(instructionsplitter_1_rn), .ReadReg2(multiplexer_1_out),
    .RegData1(registerfile_1_regdata1), .RegData2(registerfile_1_regdata2));
  ALU alu_1 (
    .Input1(registerfile_1_regdata1), .Input2(multiplexer_2_out), .Operation(control_1_aluop),
    .ALUOut(alu_1_aluout));
  Multiplexer #(.width(8)) multiplexer_2 (
    .in0(registerfile_1_regdata2), .in1(instructionsplitter_1_imm8), .out(multiplexer_2_out),
    .sel(control_1_alusrc));
  Multiplexer #(.width(8)) multiplexer_3 (
    .in0(alu_1_aluout), .in1(multiplexer_4_out), .out(multiplexer_3_out), .sel(control_1_memtoreg));
  Multiplexer #(.width(8)) multiplexer_4 (
    .in0({8{1'b0}}), .in1(Data_Memory_dout), .out(multiplexer_4_out), .sel(control_1_memread));
  Hex_Digit_Display hex_digit_display_1 (.value(multiplexer_3_out[7:4]));  // open: dp
  Hex_Digit_Display hex_digit_display_2 (.value(multiplexer_3_out[3:0]));  // open: dp

  // Notes on the sheet:
  //   Instruction_Memory
  //   Breona Pizzuta and Ben Carpenter
  //   CPU Name: Shudong-INATOR
  //   " I pledge my honor that I have abided by the Stevens Honor System"
  //   Data_Memory
endmodule

module InstructionSplitter (
  input  [15:0] Instruction,
  output [1:0] TargetReg,
  output [1:0] Rn,
  output [1:0] Rm,
  output [1:0] opcode,
  output [7:0] imm8
);


  assign imm8 = Instruction[7:0];
  assign opcode = Instruction[15:14];
  assign Rm = Instruction[9:8];
  assign Rn = Instruction[11:10];
  assign TargetReg = Instruction[13:12];
endmodule

module RegisterFile (
  input  YEPCLOCK,
  input  [1:0] WriteReg,
  input  RegWrite,
  input  [7:0] RegDataW,
  input  [1:0] ReadReg1,
  input  [1:0] ReadReg2,
  output [7:0] RegData1,
  output [7:0] RegData2
);

  wire and_1_out, and_2_out, and_3_out, and_4_out, decoder_1_out0, decoder_1_out1, decoder_1_out2,
       decoder_1_out3;
  wire [7:0] X0_q, X1_q, X2_q, X3_q;

  Decoder #(.select(2)) decoder_1 (
    .out0(decoder_1_out0), .out1(decoder_1_out1), .out2(decoder_1_out2), .out3(decoder_1_out3), .sel(WriteReg));  // open: en
  and and_1 (and_1_out, RegWrite, decoder_1_out0);
  and and_2 (and_2_out, RegWrite, decoder_1_out1);
  and and_3 (and_3_out, RegWrite, decoder_1_out2);
  and and_4 (and_4_out, RegWrite, decoder_1_out3);
  Register X0 (.D(RegDataW), .en(and_1_out), .clk(YEPCLOCK), .Q(X0_q));  // open: clr
  Register X1 (.D(RegDataW), .en(and_2_out), .clk(YEPCLOCK), .Q(X1_q));  // open: clr
  Register X2 (.D(RegDataW), .en(and_3_out), .clk(YEPCLOCK), .Q(X2_q));  // open: clr
  Register X3 (.D(RegDataW), .en(and_4_out), .clk(YEPCLOCK), .Q(X3_q));  // open: clr
  Multiplexer #(.select(2), .width(8)) multiplexer_1 (
    .in0(X0_q), .in1(X1_q), .in2(X2_q), .in3(X3_q), .out(RegData1), .sel(ReadReg1));
  Multiplexer #(.select(2), .width(8)) multiplexer_2 (
    .in0(X0_q), .in1(X1_q), .in2(X2_q), .in3(X3_q), .out(RegData2), .sel(ReadReg2));
endmodule

module ALU (
  input  [7:0] Input1,
  input  [7:0] Input2,
  input  Operation,
  output [7:0] ALUOut
);

  wire [7:0] adder_1_out, subtractor_1_out;

  Adder adder_1 (.a(Input1), .b(Input2), .out(adder_1_out));  // open: cin, cout
  Subtractor subtractor_1 (.a(Input1), .b(Input2), .out(subtractor_1_out));  // open: bin, bout
  Multiplexer #(.width(8)) multiplexer_1 (.in0(adder_1_out), .in1(subtractor_1_out), .out(ALUOut), .sel(Operation));
endmodule

module MEMORY (
  input  YEPCLOCK,
  input  [7:0] Address,
  input  MemWrite,
  input  MemRead,
  input  [7:0] WriteDataM,
  output [7:0] ReadDataM
);

  wire [7:0] Data_Memory_dout;

  RAM Data_Memory (
    .addr(Address), .we(MemWrite), .oe(MemRead), .clk(YEPCLOCK), .din(WriteDataM), .dout(Data_Memory_dout));
  Multiplexer #(.width(8)) multiplexer_1 (.in0({8{1'b0}}), .in1(Data_Memory_dout), .out(ReadDataM), .sel(MemRead));

  // Notes on the sheet:
  //   Data Memory
endmodule

module Control (
  input  [1:0] opcode,
  output MemToReg,
  output MemRead,
  output MemWrite,
  output ALUsrc,
  output ALUop,
  output RegWrite,
  output Reg2Loc
);

  wire [0:0] multiplexer_1_out;

  Multiplexer #(.select(2), .width(8)) multiplexer_1 (
    .in0(8'hd6), .in1(8'h98), .in2(8'h60), .in3(8'h40),
    .out({Reg2Loc, RegWrite, ALUop, ALUsrc, MemWrite, MemRead, MemToReg, multiplexer_1_out[0]}), .sel(opcode));

  // Notes on the sheet:
  //   Opcode Table:
  //   00: Load
  //   01: Store
  //   10: Subtract
  //   11: Add
  //   11010110
  //   10011000
  //   01100000
  //   01000000
endmodule
