// Logisim project Lab9Breona.circ as structural Verilog: 1 circuit, main circuit main
module main (
  output [7:0] OutPin
);

  wire ticktock_out;
  wire [7:0] adder_1_out, PC_q;

  Clock ticktock (.out(ticktock_out));
  Register PC (.D(adder_1_out), .en(1'b1), .clk(ticktock_out), .Q(PC_q));  // open: clr
  Adder adder_1 (.a(PC_q), .b(8'h1), .out(adder_1_out));  // open: cin, cout
  RAM ram_1 (.addr(PC_q), .we(1'b0), .oe(1'b1), .clk(ticktock_out), .dout(OutPin));  // open: din

  // Notes on the sheet:
  //   Breona Pizzuta
  //   " I pledge my honor that I have abided by the Stevens Honor System"
endmodule
